# Fritzing sketch circuit_schematic (saved by Fritzing 0.9.3b)
breadboards: 1

parts:
  LCD1 = LCD screen
  Part1 = Arduino Uno (Rev3) - ICSP
  S1 = Pushbutton [package="[THT]"]
  S2 = Pushbutton [package="[THT]"]
  S3 = Pushbutton [package="[THT]"]
  S4 = Pushbutton [package="[THT]"]
  S5 = Pushbutton [package="[THT]"]
  R1 = Resistor [tolerance=±5% resistance=1k package=THT]
  R2 = Resistor [tolerance=±20% resistance=1k package=THT]
  R3 = Resistor [tolerance=±5% resistance=1k package=THT]
  R4 = Resistor [tolerance=±5% resistance=1k package=THT]
  R5 = Resistor [tolerance=±5% resistance=1k package=THT]

nets:
  VSS: LCD1.VSS, LCD1.R/W, LCD1.LED-, Part1.GND, R1.Pin_1, R2.Pin_1, R3.Pin_1, R4.Pin_1, R5.Pin_1
  VDD: LCD1.VDD, LCD1.LED+, Part1.5V, S1.Pin_3, S1.Pin_4, S2.Pin_3, S2.Pin_4, S3.Pin_3, S3.Pin_4, S4.Pin_3, S4.Pin_4, S5.Pin_3, S5.Pin_4
  N1: LCD1.V0, Part1.D6_PWM
  N2: LCD1.RS, Part1.D12/MISO
  N3: LCD1.E, LCD1.DB0, Part1.D11_PWM/MOSI
  N4: LCD1.DB4, Part1.D5_PWM
  N5: LCD1.DB5, Part1.D4
  N6: LCD1.DB6, Part1.D3_PWM
  N7: LCD1.DB7, Part1.D2
  N8: Part1.D8, S3.Pin_1, S3.Pin_2, R3.Pin_0
  N9: Part1.D9_PWM, S5.Pin_1, S5.Pin_2, R1.Pin_0
  N10: Part1.D10_PWM/SS, S4.Pin_1, S4.Pin_2, R2.Pin_0
  N11: Part1.D13/SCK, S2.Pin_1, S2.Pin_2, R4.Pin_0
  N12: Part1.D7, S1.Pin_1, S1.Pin_2, R5.Pin_0
